// Logisim project SChema_bloc_Bastien.circ as structural Verilog: 1 circuit, main circuit main
module main (
  input  [7:0] b,
  input  Sel_i,
  output [7:0] out_3
);

  wire [7:0] adder_1_out, not_1_out, xor_1_out, xor_2_out;

  assign not_1_out = ~{8{Sel_i}};  // NOT_Gate not_1, 8 bits wide
  assign xor_1_out = b ^ {8{Sel_i}};  // XOR_Gate xor_1, 8 bits wide
  assign xor_2_out = not_1_out ^ 8'h2a;  // XOR_Gate xor_2, 8 bits wide
  Adder adder_1 (.a(xor_1_out), .b(xor_2_out), .out(adder_1_out), .cin(1'b1));  // open: cout
  Multiplexer #(.width(8), .enable("false")) multiplexer_1 (
    .in0({adder_1_out[6:0], 1'b0}), .in1(adder_1_out), .out(out_3), .sel(Sel_i));
  // Probe on out_3

  // Notes on the sheet:
  //   Attention, votre version de Logisim
  //   ne contient pas de tracker. Si vous
  //   enregistrez votre projet, toutes les
  //   informations du tracker seront
  //   définitivement effacées.
endmodule
