// Logisim project logiSchema.circ as structural Verilog: 1 circuit, main circuit main
module main (
  input  [7:0] na_i,
  input  [7:0] nb_i,
  input  Sel_i
);

  wire NOT_sel;
  wire [7:0] and_1_out;
  wire [8:0] adder_1_out, not_2_out, xor_1_out, xor_2_out;
  wire [8:1] operande_1;
  wire [9:0] operande_2;
  wire [10:0] adder_3_out;

  not not_1 (NOT_sel, Sel_i);
  // Probe on na_i
  assign not_2_out = ~{9{Sel_i}};  // NOT_Gate not_2, 9 bits wide
  assign xor_1_out = {{2{nb_i[7]}}, nb_i[6:0]} ^ {9{Sel_i}};  // XOR_Gate xor_1, 9 bits wide
  assign xor_2_out = not_2_out ^ 9'h2a;  // XOR_Gate xor_2, 9 bits wide
  // Probe on xor_1_out
  // Probe on xor_2_out
  assign and_1_out = na_i & {8{Sel_i}};  // AND_Gate and_1, 8 bits wide
  // Probe on and_1_out
  Adder #(.width(9)) adder_1 (.a(xor_1_out), .b(xor_2_out), .out(adder_1_out), .cin(1'b1));  // open: cout
  Adder adder_2 (.a({{2{na_i[7]}}, na_i[6:1]}), .b(and_1_out), .out(operande_1));  // open: cin, cout
  // Probe on {na_i[7], operande_1, na_i[0]}
  // Probe on operande_2
  Multiplexer #(.width(10), .enable("false")) multiplexer_1 (
    .in0({adder_1_out, 1'b0}), .in1({{2{adder_1_out[8]}}, adder_1_out[7:0]}), .out(operande_2), .sel(Sel_i));
  Adder #(.width(11)) adder_3 (
    .a({{2{na_i[7]}}, operande_1, na_i[0]}), .b({{2{operande_2[9]}}, operande_2[8:0]}), .out(adder_3_out));  // open: cin, cout
  // Probe on adder_3_out

  // Other names for the same wires on the sheet: nb[7:0] = nb_i; sel = Sel_i; na[7:0] = na_i;
  //   operande_1 (some bits) = {na_i[7], na_i[0]}

  // Notes on the sheet:
  //   Attention, votre version de Logisim
  //   ne contient pas de tracker. Si vous
  //   enregistrez votre projet, toutes les
  //   informations du tracker seront
  //   définitivement effacées.
  //    na * 1 ou na * 3
  //   (b-42)*2 ou (42-nb) 
  //   Sortie
endmodule
